// Logisim project Proyecto.circ as structural Verilog
module LATA (
  input  A7,
  input  A6,
  input  A5,
  input  A4,
  input  A3,
  input  A2,
  input  A1,
  input  A0,
  input  B7,
  input  B6,
  input  B5,
  input  B4,
  input  B3,
  input  B2,
  input  B1,
  input  B0,
  input  C0
);

  wire and_1_out, and_2_out, and_3_out, and_4_out, and_5_out, and_6_out, and_7_out, CH1_out, CH3_2_out,
       CH3_out, CH5_out, CH7_6_out, CH7_out, CH_out, G0_out, G1_0_out, G1_out, G2_out, G3_0_out, G3_2_out,
       G3_out, G4_out, G5_4_out, G5_out, G6_out, G7_4_out, G7_6_out, G7_out, or_1_out, or_2_out, or_3_out,
       or_4_out, or_5_out, or_6_out, or_7_out, P0_out, P1_0_out, P1_out, P2_out, P3_0_out, P3_2_out, P3_out,
       P4_out, P5_4_out, P5_out, P6_out, P7_4_out, P7_6_out, P7_out, xor_1_out, xor_2_out, xor_3_out,
       xor_4_out, xor_5_out, xor_6_out, xor_7_out, xor_8_out;

  xor xor_1 (xor_1_out, A7, B7);
  and G7 (G7_out, A7, B7);
  // XOR_Gate S7 has open pins: in0=xor_1_out, in1=CH7_out, out=open
  or P7 (P7_out, A7, B7);
  and P7_6 (P7_6_out, P6_out, P7_out);
  and and_1 (and_1_out, G6_out, P7_out);
  or or_1 (or_1_out, P6_out, G6_out);
  and CH7 (CH7_out, or_1_out, CH7_6_out);
  or G7_6 (G7_6_out, and_1_out, G7_out);
  xor xor_2 (xor_2_out, A6, B6);
  or P6 (P6_out, A6, B6);
  and G6 (G6_out, A6, B6);
  // XOR_Gate S6 has open pins: in0=xor_2_out, in1=CH7_6_out, out=open
  and P7_4 (P7_4_out, P5_4_out, P7_6_out);
  and and_2 (and_2_out, G5_4_out, P7_6_out);
  xor xor_3 (xor_3_out, A5, B5);
  or or_2 (or_2_out, P4_out, G4_out);
  or or_3 (or_3_out, P5_4_out, G5_4_out);
  or G7_4 (G7_4_out, and_2_out, G7_6_out);
  // XOR_Gate S5 has open pins: in0=xor_3_out, in1=CH5_out, out=open
  or P5 (P5_out, A5, B5);
  and G5 (G5_out, A5, B5);
  and CH5 (CH5_out, or_2_out, CH_out);
  and CH7_6 (CH7_6_out, or_3_out, CH_out);
  and P5_4 (P5_4_out, P4_out, P5_out);
  and and_3 (and_3_out, G4_out, P5_out);
  xor xor_4 (xor_4_out, A4, B4);
  or G5_4 (G5_4_out, and_3_out, G5_out);
  // XOR_Gate S4 has open pins: in0=xor_4_out, in1=CH_out, out=open
  or P4 (P4_out, A4, B4);
  and G4 (G4_out, A4, B4);
  xor xor_5 (xor_5_out, A3, B3);
  // XOR_Gate S3 has open pins: in0=xor_5_out, in1=CH3_out, out=open
  or or_4 (or_4_out, P2_out, G2_out);
  // AND_Gate P7_0 has open pins: in0=P3_0_out, in1=P7_4_out, out=open
  and and_4 (and_4_out, G3_0_out, P7_4_out);
  or P3 (P3_out, A3, B3);
  and G3 (G3_out, A3, B3);
  and CH3 (CH3_out, or_4_out, CH3_2_out);
  // OR_Gate G7_0 has open pins: in0=and_4_out, in1=G7_4_out, out=open
  or or_5 (or_5_out, P3_0_out, G3_0_out);
  and P3_2 (P3_2_out, P2_out, P3_out);
  and and_5 (and_5_out, G2_out, P3_out);
  and CH (CH_out, or_5_out, C0);
  or G3_2 (G3_2_out, and_5_out, G3_out);
  xor xor_6 (xor_6_out, A2, B2);
  or or_6 (or_6_out, P1_0_out, G1_0_out);
  // XOR_Gate S2 has open pins: in0=xor_6_out, in1=CH3_2_out, out=open
  or P2 (P2_out, A2, B2);
  and G2 (G2_out, A2, B2);
  and CH3_2 (CH3_2_out, or_6_out, C0);
  and P3_0 (P3_0_out, P1_0_out, P3_2_out);
  and and_6 (and_6_out, G1_0_out, P3_2_out);
  xor xor_7 (xor_7_out, A1, B1);
  or or_7 (or_7_out, P0_out, G0_out);
  or G3_0 (G3_0_out, and_6_out, G3_2_out);
  // XOR_Gate S1 has open pins: in0=xor_7_out, in1=CH1_out, out=open
  or P1 (P1_out, A1, B1);
  and G1 (G1_out, A1, B1);
  and CH1 (CH1_out, or_7_out, C0);
  and P1_0 (P1_0_out, P0_out, P1_out);
  and and_7 (and_7_out, G0_out, P1_out);
  xor xor_8 (xor_8_out, A0, B0);
  or G1_0 (G1_0_out, and_7_out, G1_out);
  // XOR_Gate S0 has open pins: in0=xor_8_out, in1=C0, out=open
  or P0 (P0_out, A0, B0);
  and G0 (G0_out, A0, B0);

  // Notes on the sheet:
  //   Cin
  //   FA7
  //   PL
  //   PH
  //   GL
  //   GH
  //   Cin
  //   CL
  //   Cin
  //   FA6
  //   Cin
  //   PH
  //   GH
  //   PL
  //   GL
  //   FA5
  //   CL
  //   Cin
  //   Cin
  //   Cin
  //   PL
  //   PH
  //   GH
  //   FA4
  //   GL
  //   Los C de cada FA son los Cin que están diagramados en el PDF del proyecto, es decir, dependen de los niveles más altos, hay que unirlos cuando estén hechos
  //   Cin
  //   CL
  //   FA3
  //   PH
  //   GH
  //   PL
  //   GL
  //   PL
  //   PH
  //   Cin
  //   GH
  //   CL
  //   GL
  //   FA2
  //   CL
  //   Cin
  //   Cin
  //   PL
  //   PH
  //   GL
  //   Cin
  //   GH
  //   CL
  //   FA1
  //   Cin
  //   PL
  //   PH
  //   GL
  //   CL
  //   Cin
  //   GH
  //   FA0
endmodule
